// Logisim project LAB1.circ as structural Verilog: 5 circuits, main circuit main
module main (
  output Q0,
  output Q1,
  output Q2,
  output Q3
);

  wire and_1_out, and_2_out, and_3_out, button_1_out, Cn, D0, D1, D2, D3, LD_A, LD_B, LD_OUT, not_1_out,
       not_2_out, not_3_out, not_4_out, not_5_out, not_6_out, not_7_out, not_8_out, not_9_out, not_10_out,
       not_11_out, not_12_out, not_13_out, not_14_out, not_15_out, not_16_out, not_17_out, not_18_out,
       not_19_out, not_20_out, not_21_out, not_22_out, not_23_out, not_24_out, not_25_out, not_26_out,
       not_27_out, Reset_out, S0, S1, S2;
  wire [3:0] alu_74381_lib_1_f0, REG_A_out_6, REG_B_out_6;
  wire [5:0] st_8_lib_1_q0;
  wire [15:0] rom_1_data;

  not not_1 (not_1_out, LD_B);
  Button button_1 (.out(button_1_out));
  not not_2 (not_2_out, LD_A);
  not not_3 (not_3_out, not_1_out);
  not not_4 (not_4_out, not_3_out);
  not not_5 (not_5_out, not_6_out);
  not not_6 (not_6_out, not_2_out);
  not not_7 (not_7_out, not_4_out);
  not not_8 (not_8_out, not_7_out);
  Button Reset (.out(Reset_out));
  not not_9 (not_9_out, not_5_out);
  not not_10 (not_10_out, not_9_out);
  not not_11 (not_11_out, not_8_out);
  not not_12 (not_12_out, not_11_out);
  ST_8_lib st_8_lib_1 (
    .R(Reset_out), .LD(1'b0), .C(button_1_out), .Q0(st_8_lib_1_q0[0]), .Q1(st_8_lib_1_q0[1]),
    .Q2(st_8_lib_1_q0[2]), .Q3(st_8_lib_1_q0[3]), .Q4(st_8_lib_1_q0[4]), .Q5(st_8_lib_1_q0[5]));  // open: D0, D1, D2, D3, D4, D5, D6, D7, Q6, Q7
  not not_13 (not_13_out, not_10_out);
  not not_14 (not_14_out, not_13_out);
  not not_15 (not_15_out, not_12_out);
  not not_16 (not_16_out, not_14_out);
  and and_1 (and_1_out, not_7_out, not_17_out);
  not not_17 (not_17_out, not_15_out);
  ROM #(.addrWidth(6), .dataWidth(16)) rom_1 (
    .addr(st_8_lib_1_q0),
    .data({rom_1_data[15:14], S2, S1, S0, rom_1_data[10], Cn, rom_1_data[8], D3, D2, D1, D0, LD_A, LD_B, LD_OUT, rom_1_data[0]}));
  and and_2 (and_2_out, not_9_out, not_18_out);
  not not_18 (not_18_out, not_16_out);
  REG4_lib REG_B (
    .in_5(and_1_out), .in_1(D0), .in_2(D1), .in_3(D2), .in_4(D3), .out_6(REG_B_out_6[0]),
    .out_7(REG_B_out_6[1]), .out_8(REG_B_out_6[2]), .out_9(REG_B_out_6[3]));
  REG4_lib REG_A (
    .in_5(and_2_out), .in_1(alu_74381_lib_1_f0[0]), .in_2(alu_74381_lib_1_f0[1]),
    .in_3(alu_74381_lib_1_f0[2]), .in_4(alu_74381_lib_1_f0[3]), .out_6(REG_A_out_6[0]),
    .out_7(REG_A_out_6[1]), .out_8(REG_A_out_6[2]), .out_9(REG_A_out_6[3]));
  not not_19 (not_19_out, LD_OUT);
  Hex_Digit_Display hex_digit_display_1 (.value(REG_B_out_6));  // open: dp
  not not_20 (not_20_out, not_19_out);
  not not_21 (not_21_out, not_20_out);
  Hex_Digit_Display hex_digit_display_2 (.value(REG_A_out_6));  // open: dp
  not not_22 (not_22_out, not_21_out);
  not not_23 (not_23_out, not_22_out);
  not not_24 (not_24_out, not_23_out);
  not not_25 (not_25_out, not_24_out);
  alu_74381_lib alu_74381_lib_1 (
    .Cn(Cn), .A0(REG_A_out_6[0]), .A1(REG_A_out_6[1]), .A2(REG_A_out_6[2]), .A3(REG_A_out_6[3]),
    .B0(REG_B_out_6[0]), .B1(REG_B_out_6[1]), .B2(REG_B_out_6[2]), .B3(REG_B_out_6[3]), .S0(S0), .S1(S1),
    .S2(S2), .F0(alu_74381_lib_1_f0[0]), .F1(alu_74381_lib_1_f0[1]), .F2(alu_74381_lib_1_f0[2]),
    .F3(alu_74381_lib_1_f0[3]));  // open: nP, nG
  not not_26 (not_26_out, not_25_out);
  and and_3 (and_3_out, not_22_out, not_27_out);
  not not_27 (not_27_out, not_26_out);
  // NoConnect on rom_1_data[0]
  // NoConnect on rom_1_data[8]
  // NoConnect on rom_1_data[10]
  // NoConnect on rom_1_data[14]
  // NoConnect on rom_1_data[15]
  Hex_Digit_Display hex_digit_display_3 (.value(alu_74381_lib_1_f0));  // open: dp
  REG4_lib REG_OUT (
    .in_5(and_3_out), .in_1(REG_A_out_6[0]), .in_2(REG_A_out_6[1]), .in_3(REG_A_out_6[2]),
    .in_4(REG_A_out_6[3]), .out_6(Q0), .out_7(Q1), .out_8(Q2), .out_9(Q3));
  Hex_Digit_Display hex_digit_display_4 (.value({Q3, Q2, Q1, Q0}));  // open: dp

  // Notes on the sheet:
  //   contents of rom_1 (hex, n*v repeats v):
  //   8 2 8 64 1808 2 8 b4 1808 54 1808 2 44 1208 2 4 a08 2 94 2008 2 34 1808 2 e4 1208 2 64 2008 2 b4
  //   1808 2 14 1208 2
endmodule

module ST_8_lib (
  input  R,
  input  LD,
  input  C,
  input  D0,
  input  D1,
  input  D2,
  input  D3,
  input  D4,
  input  D5,
  input  D6,
  input  D7,
  output Q0,
  output Q1,
  output Q2,
  output Q3,
  output Q4,
  output Q5,
  output Q6,
  output Q7
);

  Counter counter_1 (
    .clr(R), .load(LD), .clk(C), .D({D7, D6, D5, D4, D3, D2, D1, D0}), .Q({Q7, Q6, Q5, Q4, Q3, Q2, Q1, Q0}));  // open: up, count, carry
endmodule

module REG4_lib (
  input  in_1,
  input  in_2,
  input  in_3,
  input  in_4,
  input  in_5,
  output out_6,
  output out_7,
  output out_8,
  output out_9
);

  // Probe on {out_9, out_8, out_7, out_6}
  Register #(.width(4)) register_1 (
    .D({in_4, in_3, in_2, in_1}), .clk(in_5), .Q({out_9, out_8, out_7, out_6}));  // open: en, clr
endmodule

module alu_74381_lib (
  input  Cn,
  input  A0,
  input  A1,
  input  A2,
  input  A3,
  input  B0,
  input  B1,
  input  B2,
  input  B3,
  input  S0,
  input  S1,
  input  S2,
  output nP,
  output nG,
  output F0,
  output F1,
  output F2,
  output F3
);

  // _74381 #(.ShowInternalStructure("true")) 74381_1: pin names not known; wires that end beside it: A1, A2, B1, B2, A0, A3, B0, B3, S0, Cn, S1, nP, S2, nG, F0, F3, F1, F2
  LED LCi (.in(Cn));
  LED #(.active("false")) Lnp (.in(nP));
  LED #(.active("false")) Lng (.in(nG));
endmodule

module Test (
  output out_1,
  output out_2,
  output out_3,
  output out_4,
  output out_5,
  output out_6
);

  wire and_1_out, and_2_out, and_3_out, clock_1_out, nand_1_out, not_1_out, not_2_out, not_3_out, not_4_out,
       not_5_out, not_6_out, not_7_out, not_8_out, not_9_out, not_10_out, not_11_out, not_12_out, not_13_out,
       not_14_out, not_15_out, not_16_out, not_17_out, not_18_out, not_19_out, not_20_out, not_21_out,
       not_22_out, not_23_out, not_24_out, not_25_out, not_26_out, not_27_out, not_28_out, not_29_out,
       not_30_out, or_1_out, random_1_out, xor_1_out;

  Clock clock_1 (.out(clock_1_out));
  Random #(.width(1)) random_1 (.next(1'b1), .clk(clock_1_out), .out(random_1_out));  // open: clr
  not not_1 (not_1_out, clock_1_out);
  not not_2 (not_2_out, clock_1_out);
  not not_3 (not_3_out, not_2_out);
  not not_4 (not_4_out, clock_1_out);
  not not_5 (not_5_out, clock_1_out);
  not not_6 (not_6_out, clock_1_out);
  not not_7 (not_7_out, clock_1_out);
  not not_8 (not_8_out, not_1_out);
  not not_9 (not_9_out, not_8_out);
  not not_10 (not_10_out, not_3_out);
  not not_11 (not_11_out, not_10_out);
  not not_12 (not_12_out, not_4_out);
  not not_13 (not_13_out, not_12_out);
  not not_14 (not_14_out, not_5_out);
  not not_15 (not_15_out, not_14_out);
  not not_16 (not_16_out, not_6_out);
  not not_17 (not_17_out, not_16_out);
  not not_18 (not_18_out, not_7_out);
  not not_19 (not_19_out, not_18_out);
  not not_20 (not_20_out, not_9_out);
  not not_21 (not_21_out, not_20_out);
  not not_22 (not_22_out, not_21_out);
  not not_23 (not_23_out, not_22_out);
  not not_24 (not_24_out, not_23_out);
  not not_25 (not_25_out, not_11_out);
  not not_26 (not_26_out, not_13_out);
  not not_27 (not_27_out, not_15_out);
  not not_28 (not_28_out, not_17_out);
  not not_29 (not_29_out, not_19_out);
  not not_30 (not_30_out, not_24_out);
  and and_1 (and_1_out, clock_1_out, not_25_out);
  or or_1 (or_1_out, clock_1_out, not_26_out);
  and and_2 (and_2_out, clock_1_out, not_27_out);
  xor xor_1 (xor_1_out, clock_1_out, not_28_out);
  nand nand_1 (nand_1_out, clock_1_out, not_29_out);
  and and_3 (and_3_out, not_20_out, not_30_out);
  LED led_1 (.in(and_1_out));
  LED led_2 (.in(or_1_out));
  LED led_3 (.in(and_2_out));
  LED led_4 (.in(xor_1_out));
  LED led_5 (.in(nand_1_out));
  LED led_6 (.in(and_3_out));
  D_Flip_Flop d_ff_1 (.D(random_1_out), .clk(and_1_out), .Q(out_1));  // open: Qn, preset, reset
  D_Flip_Flop d_ff_2 (.D(random_1_out), .clk(or_1_out), .Q(out_2));  // open: Qn, preset, reset
  D_Flip_Flop d_ff_3 (.D(random_1_out), .clk(and_2_out), .Q(out_3));  // open: Qn, preset, reset
  D_Flip_Flop d_ff_4 (.D(random_1_out), .clk(xor_1_out), .Q(out_4));  // open: Qn, preset, reset
  D_Flip_Flop d_ff_5 (.D(random_1_out), .clk(nand_1_out), .Q(out_5));  // open: Qn, preset, reset
  D_Flip_Flop d_ff_6 (.D(random_1_out), .clk(and_3_out), .Q(out_6));  // open: Qn, preset, reset

  // Notes on the sheet:
  //   1 тип
  //   2 тип
  //   3 тип
  //   4 тип
  //   5 тип
  //   6 тип
endmodule
