// Logisim project lab1.circ as structural Verilog
module alu_74381_lib (
  input  Cn,
  input  A0,
  input  A1,
  input  A2,
  input  A3,
  input  B0,
  input  B1,
  input  B2,
  input  B3,
  input  S0,
  input  S1,
  input  S2,
  output nP,
  output nG,
  output F0,
  output F1,
  output F2,
  output F3
);

  // _74381 #(.ShowInternalStructure("true")) 74381_1: pin names not known; wires that end beside it: A1, A2, B1, B2, A0, A3, B0, B3, S0, Cn, S1, nP, S2, nG, F0, F3, F1, F2
  LED LCi (.in(Cn));
  LED #(.active("false")) Lnp (.in(nP));
  LED #(.active("false")) Lng (.in(nG));
endmodule

module REG4_lib (
  input  in_1,
  input  in_2,
  input  in_3,
  input  in_4,
  input  in_5,
  output out_6,
  output out_7,
  output out_8,
  output out_9
);

  // Probe on {out_9, out_8, out_7, out_6}
  Register #(.width(4)) register_1 (
    .D({in_4, in_3, in_2, in_1}), .clk(in_5), .Q({out_9, out_8, out_7, out_6}));  // open: en, clr
endmodule

module ST_8_lib (
  input  R,
  input  LD,
  input  C,
  input  D0,
  input  D1,
  input  D2,
  input  D3,
  input  D4,
  input  D5,
  input  D6,
  input  D7,
  output Q0,
  output Q1,
  output Q2,
  output Q3,
  output Q4,
  output Q5,
  output Q6,
  output Q7
);

  Counter counter_1 (
    .clr(R), .load(LD), .clk(C), .D({D7, D6, D5, D4, D3, D2, D1, D0}), .Q({Q7, Q6, Q5, Q4, Q3, Q2, Q1, Q0}));  // open: up, count, carry
endmodule
